// Logisim project Full Adders.circ as structural Verilog: 2 circuits, main circuit 3-bit full adder
module _3_bit_full_adder (
  input  X0,
  input  Carry_In,
  input  Y0,
  input  X1,
  input  Y1,
  input  X2,
  input  Y2,
  output Sum_0,
  output Sum_1,
  output Sum_2,
  output Carry_Out
);

  wire n1_bit_full_adder_1_cout, n1_bit_full_adder_2_cout;

  _1_bit_full_adder u_1_bit_full_adder_1 (.X(X0), .Y(Y0), .Cin(Carry_In), .Sum(Sum_0), .Cout(n1_bit_full_adder_1_cout));
  _1_bit_full_adder u_1_bit_full_adder_2 (
    .X(X1), .Y(Y1), .Cin(n1_bit_full_adder_1_cout), .Sum(Sum_1), .Cout(n1_bit_full_adder_2_cout));
  _1_bit_full_adder u_1_bit_full_adder_3 (
    .X(X2), .Y(Y2), .Cin(n1_bit_full_adder_2_cout), .Sum(Sum_2), .Cout(Carry_Out));
endmodule

module _1_bit_full_adder (
  input  X,
  input  Y,
  input  Cin,
  output Sum,
  output Cout
);

  wire and_1_out, and_2_out, and_3_out, and_4_out, and_5_out, and_6_out, and_7_out, not_1_out, not_2_out,
       not_3_out, not_4_out, not_5_out, not_6_out;

  not not_1 (not_1_out, X);
  not not_2 (not_2_out, Y);
  not not_3 (not_3_out, X);
  not not_4 (not_4_out, Cin);
  not not_5 (not_5_out, Y);
  not not_6 (not_6_out, Cin);
  and and_1 (and_1_out, Y, Cin);
  and and_2 (and_2_out, X, Cin);
  and and_3 (and_3_out, X, Y);
  and and_4 (and_4_out, not_1_out, not_2_out, Cin);
  and and_5 (and_5_out, not_3_out, Y, not_4_out);
  and and_6 (and_6_out, X, not_5_out, not_6_out);
  and and_7 (and_7_out, X, Y, Cin);
  or or_1 (Cout, and_1_out, and_2_out, and_3_out);
  or or_2 (Sum, and_4_out, and_5_out, and_6_out, and_7_out);
endmodule
