// Logisim project BCD to 7-seg display.circ as structural Verilog: 2 circuits, main circuit BCD - 7 seg display
module BCD___7_seg_display (
  input  X3,
  input  X2,
  input  X1,
  input  X0,
  output A,
  output F,
  output B,
  output D,
  output E,
  output C,
  output G
);

  wire and_1_out, and_2_out, and_3_out, and_4_out, and_5_out, and_6_out, and_7_out, and_8_out, and_9_out,
       and_10_out, and_11_out, and_12_out, and_13_out, and_14_out, and_15_out, and_16_out, and_17_out,
       and_18_out, and_19_out, not_1_out, not_2_out, not_3_out, not_4_out, not_5_out, not_6_out, not_7_out,
       not_8_out, not_9_out, not_10_out, not_11_out, not_12_out, not_13_out, not_14_out, not_15_out,
       not_16_out, not_17_out, not_18_out, not_19_out, not_20_out, not_21_out, not_22_out, not_23_out,
       not_24_out, not_25_out, not_26_out, not_27_out, not_28_out, not_29_out, not_30_out, not_31_out,
       not_32_out, not_33_out, not_34_out, not_35_out, not_36_out, not_37_out, not_38_out, not_39_out,
       not_40_out, not_41_out, not_42_out, not_43_out, not_44_out, not_45_out, not_46_out, not_47_out,
       not_48_out, not_49_out, not_50_out, not_51_out, not_52_out;

  not not_1 (not_1_out, X1);
  not not_2 (not_2_out, X2);
  not not_3 (not_3_out, X3);
  not not_4 (not_4_out, X0);
  not not_5 (not_5_out, X1);
  not not_6 (not_6_out, X3);
  not not_7 (not_7_out, X1);
  not not_8 (not_8_out, X2);
  not not_9 (not_9_out, X3);
  not not_10 (not_10_out, X0);
  not not_11 (not_11_out, X2);
  not not_12 (not_12_out, X3);
  not not_13 (not_13_out, X2);
  not not_14 (not_14_out, X3);
  not not_15 (not_15_out, X3);
  not not_16 (not_16_out, X1);
  not not_17 (not_17_out, X3);
  not not_18 (not_18_out, X0);
  not not_19 (not_19_out, X3);
  not not_20 (not_20_out, X1);
  not not_21 (not_21_out, X2);
  not not_22 (not_22_out, X3);
  not not_23 (not_23_out, X0);
  not not_24 (not_24_out, X1);
  not not_25 (not_25_out, X3);
  not not_26 (not_26_out, X3);
  not not_27 (not_27_out, X1);
  not not_28 (not_28_out, X2);
  not not_29 (not_29_out, X0);
  not not_30 (not_30_out, X1);
  not not_31 (not_31_out, X2);
  not not_32 (not_32_out, X3);
  not not_33 (not_33_out, X0);
  not not_34 (not_34_out, X2);
  not not_35 (not_35_out, X3);
  not not_36 (not_36_out, X0);
  not not_37 (not_37_out, X3);
  not not_38 (not_38_out, X0);
  not not_39 (not_39_out, X1);
  not not_40 (not_40_out, X2);
  not not_41 (not_41_out, X2);
  not not_42 (not_42_out, X0);
  not not_43 (not_43_out, X2);
  not not_44 (not_44_out, X3);
  not not_45 (not_45_out, X0);
  not not_46 (not_46_out, X1);
  not not_47 (not_47_out, X2);
  not not_48 (not_48_out, X3);
  not not_49 (not_49_out, X1);
  not not_50 (not_50_out, X2);
  not not_51 (not_51_out, X3);
  not not_52 (not_52_out, X3);
  and and_1 (and_1_out, X0, not_1_out, not_2_out, not_3_out);
  and and_2 (and_2_out, not_4_out, not_5_out, X2, not_6_out);
  and and_3 (and_3_out, X0, not_7_out, not_8_out, not_9_out);
  and and_4 (and_4_out, not_10_out, X1, not_11_out, not_12_out);
  and and_5 (and_5_out, X0, X1, not_13_out, not_14_out);
  and and_6 (and_6_out, X0, X1, X2, not_15_out);
  and and_7 (and_7_out, X0, not_16_out, X2, not_17_out);
  and and_8 (and_8_out, not_18_out, X1, X2, not_19_out);
  and and_9 (and_9_out, X0, not_20_out, not_21_out, not_22_out);
  and and_10 (and_10_out, not_23_out, not_24_out, X2, not_25_out);
  and and_11 (and_11_out, X0, X1, X2, not_26_out);
  and and_12 (and_12_out, X0, not_27_out, not_28_out, X3);
  and and_13 (and_13_out, not_29_out, not_30_out, not_31_out, not_32_out);
  and and_14 (and_14_out, not_33_out, X1, not_34_out, not_35_out);
  and and_15 (and_15_out, not_36_out, X1, X2, not_37_out);
  and and_16 (and_16_out, not_38_out, not_39_out, not_40_out, not_41_out, X3);
  nand nand_1 (C, not_42_out, X1, not_43_out, not_44_out);
  and and_17 (and_17_out, not_45_out, not_46_out, not_47_out, not_48_out);
  and and_18 (and_18_out, X0, not_49_out, not_50_out, not_51_out);
  and and_19 (and_19_out, X0, X1, X2, not_52_out);
  nor nor_1 (A, and_1_out, and_2_out);
  nor nor_2 (F, and_3_out, and_4_out, and_5_out, and_6_out);
  nor nor_3 (B, and_7_out, and_8_out);
  nor nor_4 (D, and_9_out, and_10_out, and_11_out, and_12_out);
  or or_1 (E, and_13_out, and_14_out, and_15_out, and_16_out);
  nor nor_5 (G, and_17_out, and_18_out, and_19_out);
endmodule

module Mod_10_Counter (
  input  Count,
  input  Enable
);

  wire and_1_out, and_2_out, and_3_out, and_4_out, bcd_7_seg_display_1_a, bcd_7_seg_display_1_b,
       bcd_7_seg_display_1_c, bcd_7_seg_display_1_d, bcd_7_seg_display_1_e, bcd_7_seg_display_1_f,
       bcd_7_seg_display_1_g, j_k_ff_1_q, j_k_ff_1_qn, j_k_ff_2_q, j_k_ff_3_q, j_k_ff_4_q, or_1_out;

  and and_1 (and_1_out, j_k_ff_1_q, j_k_ff_4_q);
  and and_2 (and_2_out, j_k_ff_4_q, j_k_ff_3_q, j_k_ff_2_q);
  J_K_Flip_Flop j_k_ff_1 (
    .J(or_1_out), .clk(Count), .K(or_1_out), .Q(j_k_ff_1_q), .Qn(j_k_ff_1_qn), .en(Enable));  // open: preset, reset
  or or_1 (or_1_out, and_1_out, and_2_out);
  and and_3 (and_3_out, j_k_ff_3_q, j_k_ff_4_q);
  BCD___7_seg_display bcd_7_seg_display_1 (
    .X3(j_k_ff_1_q), .X2(j_k_ff_2_q), .X1(j_k_ff_3_q), .X0(j_k_ff_4_q), .A(bcd_7_seg_display_1_a),
    .F(bcd_7_seg_display_1_f), .B(bcd_7_seg_display_1_b), .D(bcd_7_seg_display_1_d),
    .E(bcd_7_seg_display_1_e), .C(bcd_7_seg_display_1_c), .G(bcd_7_seg_display_1_g));
  J_K_Flip_Flop j_k_ff_2 (
    .J(and_3_out), .clk(Count), .K(and_3_out), .Q(j_k_ff_2_q), .en(Enable));  // open: Qn, preset, reset
  and and_4 (and_4_out, j_k_ff_1_qn, j_k_ff_4_q);
  J_K_Flip_Flop j_k_ff_3 (
    .J(and_4_out), .clk(Count), .K(and_4_out), .Q(j_k_ff_3_q), .en(Enable));  // open: Qn, preset, reset
  J_K_Flip_Flop j_k_ff_4 (.J(1'b1), .clk(Count), .K(1'b1), .Q(j_k_ff_4_q), .en(Enable));  // open: Qn, preset, reset
  _7_Segment_Display u_7_segment_display_1 (
    .g(bcd_7_seg_display_1_g), .f(bcd_7_seg_display_1_f), .a(bcd_7_seg_display_1_a),
    .b(bcd_7_seg_display_1_b), .e(bcd_7_seg_display_1_e), .d(bcd_7_seg_display_1_d), .c(bcd_7_seg_display_1_c));  // open: dp
endmodule
